# Fritzing sketch infopanel (saved by Fritzing 0.9.4)
circuit board: 7.91225cm x 5.67216cm

parts:
  R_Speaker = female pin header, 2 pins [form="♀ (female)"]
  Cpwr = Electrolytic Capacitor [capacitance=10µF package="100 mil [THT, electrolytic]"]
  NJM_2113 = IC, DIP package, 8 pins [chip_label=IC]
  Ri = Resistor [tolerance=±5% resistance=3.3k package=THT]
  Ci = Ceramic Capacitor [capacitance=0.1µF package="100 mil [THT, multilayer]"]
  C1 = Electrolytic Capacitor [capacitance=1µF package="100 mil [THT, electrolytic]"]
  C2 = Electrolytic Capacitor [capacitance=4.7µF package="100 mil [THT, electrolytic]"]
  R1 = Resistor [tolerance=±5% resistance=68k package=THT]
  Audio_R = female pin header, 2 pins [form="♀ (female)"]
  NJM_2113_2 = IC, DIP package, 8 pins [chip_label=IC]
  L_Speaker = female pin header, 2 pins [form="♀ (female)"]
  Ri_2 = Resistor [tolerance=±5% resistance=3.3k package=THT]
  C1_2 = Electrolytic Capacitor [capacitance=1µF package="100 mil [THT, electrolytic]"]
  C2_2 = Electrolytic Capacitor [capacitance=4.7µF package="100 mil [THT, electrolytic]"]
  R1_2 = Resistor [tolerance=±5% resistance=68k package=THT]
  Audio_L = female pin header, 2 pins [form="♀ (female)"]
  Buttons_GND = male pin header, 8 pins [form="♂ (male)"]
  Buttons = male pin header, 8 pins [form="♂ (male)"]
  Ci_2 = Ceramic Capacitor [capacitance=0.1µF package="100 mil [THT, multilayer]"]
  Amp_Off/On = female pin header, 2 pins [form="♀ (female)"]
  RPi_even = female pin header, 20 pins [form="♀ (female)"]
  RPi_odd = female pin header, 20 pins [form="♀ (female)"]
  ULN2804 = ULN2803A [package=THT]
  R13 = Resistor [tolerance=±5% resistance=330 package=THT]
  R14 = Resistor [tolerance=±5% resistance=330 package=THT]
  R15 = Resistor [tolerance=±5% resistance=330 package=THT]
  R16 = Resistor [tolerance=±5% resistance=330 package=THT]
  R17 = Resistor [tolerance=±5% resistance=330 package=THT]
  R18 = Resistor [tolerance=±5% resistance=330 package=THT]
  R19 = Resistor [tolerance=±5% resistance=330 package=THT]
  R20 = Resistor [tolerance=±5% resistance=330 package=THT]
  LED+ = male pin header, 8 pins [form="♂ (male)"]
  LED- = male pin header, 8 pins [form="♂ (male)"]
  Pad1 = Pad [width=1.6631354434239665 height=1.8155456293663628 connect=center]
  Pad2 = Pad [width=1.6631354434239665 height=1.8155456293663628 connect=center]
  Pad3 = Pad [width=1.6631354434239665 height=1.8155456293663628 connect=center]
  Pad4 = Pad [width=1.6631354434239665 height=1.8155456293663628 connect=center]
  Pad5 = Pad [width=1.6631354434239665 height=1.8155456293663628 connect=center]
  Pad6 = Pad [width=1.6631354434239665 height=1.8155456293663628 connect=center]
  Pad7 = Pad [width=1.6631354434239665 height=1.8155456293663628 connect=center]
  Pad8 = Pad [width=1.6631354434239665 height=1.8155456293663628 connect=center]
  Pad9 = Pad [width=1.6631354434239665 height=1.8155456293663628 connect=center]
  Pad10 = Pad [width=1.6631354434239665 height=1.8155456293663628 connect=center]
  Pad11 = Pad [width=1.6631354434239665 height=1.8155456293663628 connect=center]
  Pad12 = Pad [width=1.6631354434239665 height=1.8155456293663628 connect=center]
  Pad13 = Pad [width=1.6631354434239665 height=1.8155456293663628 connect=center]
  Pad14 = Pad [width=1.6631354434239665 height=1.8155456293663628 connect=center]
  Pad15 = Pad [width=1.6631354434239665 height=1.8155456293663628 connect=center]
  Pad16 = Pad [width=1.6631354434239665 height=1.8155456293663628 connect=center]
  S1 = Pushbutton [package=THT]  # not connected
  S2 = Pushbutton [package=THT]  # not connected
  S3 = Pushbutton [package=THT]  # not connected
  S4 = Pushbutton [package=THT]  # not connected
  S5 = Pushbutton [package=THT]  # not connected
  S6 = Pushbutton [package=THT]  # not connected
  S7 = Pushbutton [package=THT]  # not connected
  S8 = Pushbutton [package=THT]  # not connected
  LED1 = LED - 3mm [color="Red (633nm)" package="3 mm [THT]"]  # not connected
  LED2 = LED - 3mm [color="Red (633nm)" package="3 mm [THT]"]  # not connected
  LED3 = LED - 3mm [color="Red (633nm)" package="3 mm [THT]"]  # not connected
  LED4 = LED - 3mm [color="Red (633nm)" package="3 mm [THT]"]  # not connected
  LED5 = LED - 3mm [color="Red (633nm)" package="3 mm [THT]"]  # not connected
  LED6 = LED - 3mm [color="Red (633nm)" package="3 mm [THT]"]  # not connected
  LED7 = LED - 3mm [color="Red (633nm)" package="3 mm [THT]"]  # not connected
  LED8 = LED - 3mm [color="Red (633nm)" package="3 mm [THT]"]  # not connected
  SPKR1 = Loudspeaker  # not connected
  SPKR2 = Loudspeaker  # not connected
  MCU1 = Raspberry Pi Zero  # not connected

nets:
  N1: R_Speaker.pin1, NJM_2113.pin8
  N2: R_Speaker.pin2, NJM_2113.pin5, R1.Pin_1
  GND: Cpwr.-, NJM_2113.pin7, C1.-, C2.-, NJM_2113_2.pin7, C1_2.-, C2_2.-, Buttons_GND.pin1, Buttons_GND.pin2, Buttons_GND.pin3, Buttons_GND.pin4, Buttons_GND.pin5, Buttons_GND.pin6, Buttons_GND.pin7, Buttons_GND.pin8, RPi_even.pin3, RPi_odd.pin5, RPi_odd.pin20, ULN2804.0V
  5V: Cpwr.+, NJM_2113.pin6, NJM_2113_2.pin6, RPi_even.pin1, RPi_even.pin2, LED+.pin1, LED+.pin2, LED+.pin3, LED+.pin4, LED+.pin5, LED+.pin6, LED+.pin7, LED+.pin8
  N3: NJM_2113.pin1, NJM_2113_2.pin1, Amp_Off/On.pin1
  N4: NJM_2113.pin2, C2.+
  N5: NJM_2113.pin3, C1.+
  N6: NJM_2113.pin4, Ri.Pin_1, R1.Pin_0
  N7: Ri.Pin_0, Ci.1
  N8: Ci.0, Audio_R.pin2
  N9: Audio_R.pin1, RPi_even.pin6
  N10: NJM_2113_2.pin2, C2_2.+
  N11: NJM_2113_2.pin3, C1_2.+
  N12: NJM_2113_2.pin4, Ri_2.Pin_1, R1_2.Pin_0
  N13: NJM_2113_2.pin5, L_Speaker.pin2, R1_2.Pin_1
  N14: NJM_2113_2.pin8, L_Speaker.pin1
  N15: Ri_2.Pin_0, Ci_2.1
  N16: Audio_L.pin1, RPi_odd.pin17
  N17: Audio_L.pin2, Ci_2.0
  N18: Buttons.pin1, RPi_even.pin4
  N19: Buttons.pin2, RPi_even.pin5
  N20: Buttons.pin3, RPi_even.pin8
  N21: Buttons.pin4, RPi_even.pin9
  N22: Buttons.pin5, RPi_even.pin11
  N23: Buttons.pin6, RPi_even.pin12
  N24: Buttons.pin7, RPi_even.pin13
  N25: Buttons.pin8, RPi_even.pin16
  N26: Amp_Off/On.pin2, RPi_even.pin18
  N27: RPi_even.pin7, Pad14.pad
  N28: RPi_even.pin10, Pad13.pad
  N29: RPi_even.pin14, Pad12.pad
  N30: RPi_even.pin15, Pad11.pad
  N31: RPi_even.pin17, Pad10.pad
  N32: RPi_even.pin19, Pad9.pad
  N33: RPi_even.pin20, Pad8.pad
  N34: RPi_odd.pin1, RPi_odd.pin2, ULN2804.In_8
  N35: RPi_odd.pin3, ULN2804.In_7
  N36: RPi_odd.pin4, ULN2804.In_6
  N37: RPi_odd.pin6, ULN2804.In_5
  N38: RPi_odd.pin7, ULN2804.In_4
  N39: RPi_odd.pin8, ULN2804.In_3
  N40: RPi_odd.pin9, Pad16.pad
  N41: RPi_odd.pin10, ULN2804.In_2
  N42: RPi_odd.pin11, ULN2804.In_1
  N43: RPi_odd.pin12, Pad1.pad
  N44: RPi_odd.pin13, Pad2.pad
  N45: RPi_odd.pin14, Pad3.pad
  N46: RPi_odd.pin15, Pad4.pad
  N47: RPi_odd.pin16, Pad5.pad
  N48: RPi_odd.pin18, Pad6.pad
  N49: RPi_odd.pin19, Pad7.pad
  N50: ULN2804.COM_-_Common, Pad15.pad
  N51: ULN2804.Out_8, R19.Pin_0
  N52: ULN2804.Out_7, R18.Pin_0
  N53: ULN2804.Out_6, R14.Pin_0
  N54: ULN2804.Out_5, R16.Pin_0
  N55: ULN2804.Out_4, R17.Pin_0
  N56: ULN2804.Out_3, R15.Pin_0
  N57: ULN2804.Out_2, R20.Pin_0
  N58: ULN2804.Out_1, R13.Pin_0
  N59: R13.Pin_1, LED-.pin8
  N60: R14.Pin_1, LED-.pin3
  N61: R15.Pin_1, LED-.pin6
  N62: R16.Pin_1, LED-.pin4
  N63: R17.Pin_1, LED-.pin5
  N64: R18.Pin_1, LED-.pin2
  N65: R19.Pin_1, LED-.pin1
  N66: R20.Pin_1, LED-.pin7

notes:
  Odd pins (p = n*2 - 1)
  Even pins (p = n*2)
  LED
  GND
  +   -
  BTN
  Amp
  Off/On
  Non-PCB components
  ----->
  1  18
  9  10
